# Fritzing sketch 23LC1024 SRAM SPI (saved by Fritzing 0.9.3b)
breadboards: 1

parts:
  ATMega328p = Arduino Nano (Rev3.0)
  23LC1024_SPI_SRAM = IC, DIP package, 8 pins [chip_label=IC]

nets:
  N1: ATMega328p.GND, 23LC1024_SPI_SRAM.pin4
  N2: ATMega328p.D10, 23LC1024_SPI_SRAM.pin1
  N3: ATMega328p.D11/MOSI, 23LC1024_SPI_SRAM.pin5
  N4: ATMega328p.D12/MISO, 23LC1024_SPI_SRAM.pin2
  N5: ATMega328p.5V, 23LC1024_SPI_SRAM.pin7, 23LC1024_SPI_SRAM.pin8
  N6: ATMega328p.D13/SCK, 23LC1024_SPI_SRAM.pin6

notes:
  Done by : Shankar
